// Logisim project jrmips-mbo10.circ as structural Verilog
module main (
);

  wire and_1_out, Branch_out, Clock_out, Decoder_alusrc, Decoder_branch, Decoder_halt, Decoder_jump,
       Decoder_memread, Decoder_memtoreg, Decoder_memwrite, Decoder_put, Decoder_regwrite, Decoder_shift,
       Fields_subop, not_1_out, not_2_out, or_1_out, or_2_out, or_3_out, or_4_out;
  wire [1:0] Decoder_aluop2;
  wire [2:0] Fields_rs, Fields_rt;
  wire [3:0] Fields_opcode, Fields_shamt, register_1_q_2;
  wire [7:0] adder_1_out, Fields_imm, multiplexer_1_out, multiplexer_2_out, PC_q, Registers_read_data_1,
       Registers_read_data_2;
  wire [11:0] register_1_q;
  wire [15:0] ALU_result, multiplexer_3_out, multiplexer_4_out, multiplexer_5_out, multiplexer_6_out,
       ram_1_data, rom_1_data, Shifter_output, Sign_Extend_2_output, Sign_Extend_output;
  wire [15:8] Registers_read_data_1_2, Registers_read_data_2_2;

  not not_1 (not_1_out, Decoder_halt);
  LED Halt (.in(Decoder_halt));
  Register PC (.D(multiplexer_1_out), .en(not_1_out), .Q(PC_q), .clk(Clock_out));  // open: clr
  Clock Clock (.out(Clock_out));
  or or_1 (or_1_out, not_2_out, or_2_out);
  Adder adder_1 (.a(8'h1), .b(PC_q), .out(adder_1_out), .cin(1'b0));  // open: cout
  Multiplexer #(.width(8), .enable("false")) multiplexer_1 (
    .in0(adder_1_out), .in1(multiplexer_2_out), .out(multiplexer_1_out), .sel(or_3_out));
  not not_2 (not_2_out, Decoder_jump);
  or or_2 (or_2_out, Decoder_aluop2[1], Decoder_aluop2[0]);
  Multiplexer #(.width(8), .enable("false")) multiplexer_2 (
    .in0(Registers_read_data_1), .in1(Fields_imm), .out(multiplexer_2_out), .sel(or_1_out));
  or or_3 (or_3_out, and_1_out, Decoder_jump);
  Shifter Shifter (
    .Shamt(Fields_shamt), .Rt({Registers_read_data_2_2, Registers_read_data_2}),
    .Rs({Registers_read_data_1_2, Registers_read_data_1}), .SubOp(Fields_subop),
    .Immediate(Fields_opcode[0]), .Output(Shifter_output));
  ROM #(.dataWidth(16)) rom_1 (.addr(PC_q), .data(rom_1_data), .sel(1'b1));
  Register #(.width(16)) register_1 (
    .D({Registers_read_data_1_2, Registers_read_data_1}), .en(Decoder_put),
    .Q({register_1_q_2, register_1_q}), .clk(Clock_out));  // open: clr
  Hex_Digit_Display hex_digit_display_1 (.value(register_1_q_2));  // open: dp
  and and_1 (and_1_out, or_4_out, Decoder_branch);
  Fields Fields (
    .Input(rom_1_data), .Opcode(Fields_opcode), .Subop(Fields_subop), .Shamt(Fields_shamt), .Imm(Fields_imm),
    .RS(Fields_rs), .RT(Fields_rt));
  Hex_Digit_Display hex_digit_display_2 (.value(register_1_q[11:8]));  // open: dp
  Hex_Digit_Display hex_digit_display_3 (.value(register_1_q[7:4]));  // open: dp
  or or_4 (or_4_out, Branch_out, Decoder_jump);
  Decoder Decoder (
    .OPC0(Fields_opcode[3]), .OPC1(Fields_opcode[2]), .OPC2(Fields_opcode[1]), .OPC3(Fields_opcode[0]),
    .SubOp(Fields_subop), .Jump(Decoder_jump), .Shift(Decoder_shift), .Halt(Decoder_halt),
    .Branch(Decoder_branch), .Put(Decoder_put), .MemToReg(Decoder_memtoreg), .RegWrite(Decoder_regwrite),
    .ALUsrc(Decoder_alusrc), .ALUOP1(Decoder_aluop2[1]), .ALUOP2(Decoder_aluop2[0]),
    .MemWrite(Decoder_memwrite), .MemRead(Decoder_memread));
  Sign_Extend Sign_Extend (.Input(Fields_imm), .Sign(Fields_subop), .Op(Fields_opcode), .Output(Sign_Extend_output));
  Hex_Digit_Display hex_digit_display_4 (.value(register_1_q[3:0]));  // open: dp
  Register_File Registers (
    .Read_1(Fields_rs), .Read_2(Fields_rt), .Write(Fields_rs), .Write_Data(multiplexer_4_out),
    .Clock(Clock_out), .RegWrite(Decoder_regwrite),
    .Read_Data_1({Registers_read_data_1_2, Registers_read_data_1}),
    .Read_Data_2({Registers_read_data_2_2, Registers_read_data_2}));
  Sign_Extend Sign_Extend_2 (.Input(adder_1_out), .Sign(1'b0), .Op(4'b0000), .Output(Sign_Extend_2_output));
  Branch Branch (.RS({Registers_read_data_1_2, Registers_read_data_1}), .ALU_OP(Decoder_aluop2), .Out(Branch_out));
  Multiplexer #(.width(16), .enable("false")) multiplexer_3 (
    .in0({Registers_read_data_2_2, Registers_read_data_2}), .in1(Sign_Extend_output),
    .out(multiplexer_3_out), .sel(Decoder_alusrc));
  Multiplexer #(.width(16), .enable("false")) multiplexer_4 (
    .in0(multiplexer_5_out), .in1(Shifter_output), .out(multiplexer_4_out), .sel(Decoder_shift));
  ALU ALU (
    .A({Registers_read_data_1_2, Registers_read_data_1}), .B(multiplexer_3_out), .Operation(Decoder_aluop2),
    .Result(ALU_result));
  Multiplexer #(.width(16), .enable("false")) multiplexer_5 (
    .in0(multiplexer_6_out), .in1(Sign_Extend_2_output), .out(multiplexer_5_out), .sel(Decoder_jump));
  RAM #(.dataWidth(16), .bus("separate")) ram_1 (
    .addr(Registers_read_data_2), .din({Registers_read_data_1_2, Registers_read_data_1}), .data(ram_1_data),
    .str(Decoder_memwrite), .clk(Clock_out), .ld(Decoder_memread));  // open: sel, clr
  Multiplexer #(.width(16), .enable("false")) multiplexer_6 (
    .in0(ram_1_data), .in1(ALU_result), .out(multiplexer_6_out), .sel(Decoder_memtoreg));

  // Notes on the sheet:
  //   Michael Oles
  //   mbo10@pitt.edu
  //   contents of rom_1 (hex, n*v repeats v):
  //   1001 7000 2002 1241 1200 23e0 9202 6000 14*0 2003 15*0 5401
endmodule

module Register_File (
  input  [2:0] Read_1,
  input  [2:0] Read_2,
  input  RegWrite,
  input  [2:0] Write,
  input  Clock,
  input  [15:0] Write_Data,
  output [15:0] Read_Data_1,
  output [15:0] Read_Data_2
);

  wire demultiplexer_1_out0, demultiplexer_1_out1, demultiplexer_1_out2, demultiplexer_1_out3,
       demultiplexer_1_out4, demultiplexer_1_out5, demultiplexer_1_out6, demultiplexer_1_out7;
  wire [15:0] Reg_1_q, Reg_2_q, Reg_3_q, Reg_4_q, Reg_5_q, Reg_7_q, Reg_8_q;

  Demultiplexer #(.select(3), .disabled(0)) demultiplexer_1 (
    .out0(demultiplexer_1_out0), .out1(demultiplexer_1_out1), .out2(demultiplexer_1_out2),
    .out3(demultiplexer_1_out3), .out4(demultiplexer_1_out4), .out5(demultiplexer_1_out5),
    .out6(demultiplexer_1_out6), .out7(demultiplexer_1_out7), .in(1'b1), .sel(Write), .en(RegWrite));
  Register #(.width(16)) Reg_1 (.D(Write_Data), .en(demultiplexer_1_out0), .Q(Reg_1_q), .clk(Clock));  // open: clr
  Register #(.width(16)) Reg_2 (.D(Write_Data), .en(demultiplexer_1_out1), .Q(Reg_2_q), .clk(Clock));  // open: clr
  Register #(.width(16)) Reg_3 (.D(Write_Data), .en(demultiplexer_1_out2), .Q(Reg_3_q), .clk(Clock));  // open: clr
  Register #(.width(16)) Reg_4 (.D(Write_Data), .en(demultiplexer_1_out3), .Q(Reg_4_q), .clk(Clock));  // open: clr
  Register #(.width(16)) Reg_5 (.D(Write_Data), .en(demultiplexer_1_out4), .Q(Reg_5_q), .clk(Clock));  // open: clr
  Register #(.width(16)) Reg_6 (.D(Write_Data), .en(demultiplexer_1_out5), .Q(Reg_5_q), .clk(Clock));  // open: clr
  Register #(.width(16)) Reg_7 (.D(Write_Data), .en(demultiplexer_1_out6), .Q(Reg_7_q), .clk(Clock));  // open: clr
  Register #(.width(16)) Reg_8 (.D(Write_Data), .en(demultiplexer_1_out7), .Q(Reg_8_q), .clk(Clock));  // open: clr
  Multiplexer #(.select(3), .width(16), .enable("false")) multiplexer_1 (
    .in0(Reg_1_q), .in1(Reg_2_q), .in2(Reg_3_q), .in3(Reg_4_q), .in4(Reg_5_q), .in5(Reg_5_q), .in6(Reg_7_q),
    .in7(Reg_8_q), .out(Read_Data_1), .sel(Read_1));
  Multiplexer #(.select(3), .width(16), .enable("false")) multiplexer_2 (
    .in0(Reg_1_q), .in1(Reg_2_q), .in2(Reg_3_q), .in3(Reg_4_q), .in4(Reg_5_q), .in5(Reg_5_q), .in6(Reg_7_q),
    .in7(Reg_8_q), .out(Read_Data_2), .sel(Read_2));
endmodule

module Fields (
  input  [15:0] Input,
  output [3:0] Opcode,
  output Subop,
  output [3:0] Shamt,
  output [7:0] Imm,
  output [2:0] RS,
  output [2:0] RT
);


  assign Imm = Input[8:1];
  assign Opcode = Input[15:12];
  assign RS = Input[11:9];
  assign RT = Input[8:6];
  assign Shamt = Input[4:1];
  assign Subop = Input[0];
endmodule

module ALU (
  input  [1:0] Operation,
  input  [15:0] A,
  input  [15:0] B,
  output [15:0] Result
);

  wire [15:0] adder_1_out, and_1_out, nor_1_out, subtractor_1_out;

  Adder #(.width(16)) adder_1 (.a(A), .b(B), .out(adder_1_out), .cin(1'b0));  // open: cout
  Subtractor #(.width(16)) subtractor_1 (.a(A), .b(B), .out(subtractor_1_out), .bin(1'b0));  // open: bout
  assign nor_1_out = ~(A | B);  // NOR_Gate nor_1, 16 bits wide
  assign and_1_out = A & B;  // AND_Gate and_1, 16 bits wide
  Multiplexer #(.select(2), .width(16), .enable("false")) multiplexer_1 (
    .in0(adder_1_out), .in1(subtractor_1_out), .in2(nor_1_out), .in3(and_1_out), .out(Result), .sel(Operation));
endmodule

module Decoder (
  input  OPC0,
  input  OPC1,
  input  OPC2,
  input  OPC3,
  input  SubOp,
  output Jump,
  output Shift,
  output Halt,
  output Branch,
  output Put,
  output MemToReg,
  output RegWrite,
  output ALUsrc,
  output ALUOP1,
  output ALUOP2,
  output MemWrite,
  output MemRead
);

  wire and_1_out, and_2_out, and_3_out, and_4_out, and_8_out, and_9_out, and_10_out, and_11_out, and_12_out,
       and_13_out, and_14_out, and_15_out, and_16_out, and_17_out, and_18_out, and_19_out, and_20_out,
       not_1_out, not_2_out, not_3_out, not_4_out, not_5_out, not_6_out, not_7_out, not_8_out, not_9_out,
       not_10_out, not_11_out, not_12_out, not_13_out, not_14_out, not_15_out, not_16_out, not_17_out,
       not_18_out, not_19_out, not_20_out, not_21_out, not_22_out, not_23_out, not_24_out, not_25_out,
       not_26_out, not_27_out, not_28_out, not_29_out, not_30_out, not_31_out, not_32_out, not_33_out,
       not_34_out, not_35_out, not_36_out, not_37_out, not_38_out, not_39_out, not_40_out, not_41_out,
       not_42_out, not_43_out;

  not not_1 (not_1_out, OPC2);
  not not_2 (not_2_out, OPC3);
  not not_3 (not_3_out, OPC0);
  not not_4 (not_4_out, OPC1);
  not not_5 (not_5_out, OPC0);
  not not_6 (not_6_out, OPC2);
  not not_7 (not_7_out, OPC3);
  not not_8 (not_8_out, OPC3);
  not not_9 (not_9_out, OPC1);
  not not_10 (not_10_out, OPC0);
  not not_11 (not_11_out, OPC1);
  not not_12 (not_12_out, OPC3);
  not not_13 (not_13_out, OPC0);
  not not_14 (not_14_out, OPC1);
  not not_15 (not_15_out, OPC0);
  not not_16 (not_16_out, OPC2);
  not not_17 (not_17_out, OPC3);
  not not_18 (not_18_out, OPC0);
  not not_19 (not_19_out, OPC2);
  not not_20 (not_20_out, SubOp);
  not not_21 (not_21_out, OPC2);
  not not_22 (not_22_out, OPC1);
  not not_23 (not_23_out, OPC3);
  not not_24 (not_24_out, OPC0);
  not not_25 (not_25_out, OPC2);
  not not_26 (not_26_out, OPC3);
  not not_27 (not_27_out, OPC3);
  not not_28 (not_28_out, OPC1);
  not not_29 (not_29_out, OPC0);
  not not_30 (not_30_out, OPC2);
  not not_31 (not_31_out, OPC3);
  not not_32 (not_32_out, SubOp);
  not not_33 (not_33_out, OPC0);
  not not_34 (not_34_out, OPC0);
  not not_35 (not_35_out, OPC3);
  not not_36 (not_36_out, SubOp);
  not not_37 (not_37_out, OPC1);
  not not_38 (not_38_out, OPC3);
  not not_39 (not_39_out, OPC0);
  not not_40 (not_40_out, OPC2);
  not not_41 (not_41_out, OPC0);
  not not_42 (not_42_out, OPC2);
  not not_43 (not_43_out, SubOp);
  and and_1 (and_1_out, OPC0, OPC1, not_1_out);
  and and_2 (and_2_out, OPC0, OPC1, not_2_out);
  and and_3 (and_3_out, not_3_out, not_4_out, OPC2, OPC3);
  and and_4 (and_4_out, not_5_out, OPC1, not_6_out, not_7_out);
  and and_5 (Halt, OPC1, OPC2, not_8_out);
  and and_6 (Branch, OPC0, not_9_out);
  and and_7 (Put, not_10_out, OPC1, OPC2, OPC3);
  or or_1 (MemToReg, not_11_out, not_12_out, SubOp, OPC2, OPC0);
  and and_8 (and_8_out, not_13_out, not_14_out);
  and and_9 (and_9_out, not_15_out, not_16_out, not_17_out);
  and and_10 (and_10_out, not_18_out, not_19_out, not_20_out);
  and and_11 (and_11_out, OPC0, OPC1, not_21_out, OPC3);
  and and_12 (and_12_out, not_22_out, OPC2, not_23_out);
  and and_13 (and_13_out, not_24_out, not_25_out, not_26_out);
  and and_14 (and_14_out, OPC1, OPC2, not_27_out);
  and and_15 (and_15_out, OPC0, not_28_out, OPC2);
  and and_16 (and_16_out, not_29_out, not_30_out, not_31_out, not_32_out);
  and and_17 (and_17_out, not_33_out, OPC3, SubOp);
  and and_18 (and_18_out, not_34_out, OPC1, not_35_out, not_36_out);
  and and_19 (and_19_out, OPC0, not_37_out, OPC3);
  and and_20 (and_20_out, OPC0, OPC1, OPC2, not_38_out);
  and and_21 (MemWrite, not_39_out, OPC1, not_40_out, OPC3, SubOp);
  and and_22 (MemRead, not_41_out, OPC1, not_42_out, OPC3, not_43_out);
  or or_2 (Jump, and_1_out, and_2_out);
  or or_3 (Shift, and_3_out, and_4_out);
  or or_4 (RegWrite, and_8_out, and_9_out, and_10_out, and_11_out);
  or or_5 (ALUsrc, and_12_out, OPC0);
  or or_6 (ALUOP1, and_13_out, and_14_out, and_15_out);
  or or_7 (ALUOP2, and_16_out, and_17_out, and_18_out, and_19_out, and_20_out);
endmodule

module Shifter (
  input  [3:0] Shamt,
  input  [15:0] Rt,
  input  [15:0] Rs,
  input  SubOp,
  input  Immediate,
  output [15:0] Output
);

  wire not_1_out;
  wire [3:0] multiplexer_1_out, multiplexer_2_out;
  wire [15:0] shifter_1_out, shifter_2_out;

  not not_1 (not_1_out, Immediate);
  Multiplexer #(.width(4), .enable("false")) multiplexer_1 (
    .in0(Shamt), .in1(Rt[3:0]), .out(multiplexer_1_out), .sel(not_1_out));
  Multiplexer #(.width(4), .enable("false")) multiplexer_2 (
    .in0(Shamt), .in1(Rt[3:0]), .out(multiplexer_2_out), .sel(not_1_out));
  Shifter_part #(.width(16)) shifter_1 (.in(Rs), .\dist (multiplexer_1_out), .out(shifter_1_out));
  Shifter_part #(.width(16), .shift("lr")) shifter_2 (.in(Rs), .\dist (multiplexer_2_out), .out(shifter_2_out));
  Multiplexer #(.width(16), .enable("false")) multiplexer_3 (
    .in0(shifter_1_out), .in1(shifter_2_out), .out(Output), .sel(SubOp));
endmodule

module Branch (
  input  [15:0] RS,
  input  [1:0] ALU_OP,
  output Out
);

  wire comparator_1_eq, comparator_1_gt, comparator_1_lt, not_1_out;

  Comparator #(.width(16)) comparator_1 (
    .a(RS), .b({16{1'b0}}), .gt(comparator_1_gt), .eq(comparator_1_eq), .lt(comparator_1_lt));
  not not_1 (not_1_out, comparator_1_eq);
  Multiplexer #(.select(2), .enable("false")) multiplexer_1 (
    .in0(comparator_1_gt), .in1(comparator_1_lt), .in2(not_1_out), .in3(comparator_1_eq), .out(Out),
    .sel(ALU_OP));
endmodule

module Sign_Extend (
  input  [3:0] Op,
  input  Sign,
  input  [7:0] Input,
  output [15:0] Output
);

  wire and_1_out, not_1_out, not_2_out, not_3_out, not_4_out;
  wire [15:0] bit_extender_1_out, bit_extender_2_out;

  assign bit_extender_1_out = {{8{1'b0}}, Input};  // Bit_Extender bit_extender_1
  assign bit_extender_2_out = {{8{Input[7]}}, Input};  // Bit_Extender bit_extender_2
  not not_1 (not_1_out, Op[2]);
  not not_2 (not_2_out, Op[0]);
  not not_3 (not_3_out, Op[3]);
  not not_4 (not_4_out, Sign);
  and and_1 (and_1_out, not_4_out, not_3_out, not_1_out, Op[1], not_2_out);
  Multiplexer #(.width(16), .enable("false")) multiplexer_1 (
    .in0(bit_extender_1_out), .in1(bit_extender_2_out), .out(Output), .sel(and_1_out));
endmodule
