// Logisim project jrmips-mbo10test.circ as structural Verilog
module main (
);

  wire Clock_out, Decoder_p4, Decoder_p5, Decoder_p7, Decoder_p8, Decoder_p9, Decoder_p10, Decoder_p13,
       Fields_subop, not_1_out;
  wire [1:0] Decoder_p11;
  wire [2:0] Fields_rs, Fields_rt;
  wire [3:0] Fields_opcode, Fields_shamt, register_1_q, register_1_q_2;
  wire [7:0] adder_1_out, ALU_result, Fields_imm, multiplexer_1_out, PC_q;
  wire [15:0] Decoder_p6, multiplexer_2_out, multiplexer_3_out, ram_1_data, Registers_read_data_1,
       rom_1_data, Sign_Extend_output;
  wire [15:8] ALU_result_2, register_1_q_3;

  LED Halt (.in(Decoder_p4));
  not not_1 (not_1_out, Decoder_p4);
  Clock Clock (.out(Clock_out));
  Adder adder_1 (.a(8'h1), .b(PC_q), .out(adder_1_out), .cin(1'b0));  // open: cout
  Register PC (.D(multiplexer_1_out), .en(not_1_out), .Q(PC_q), .clk(Clock_out));  // open: clr
  Multiplexer #(.width(8), .enable("false")) multiplexer_1 (
    .in0(adder_1_out), .in1(Fields_imm), .out(multiplexer_1_out), .sel(Decoder_p5));
  ROM #(.dataWidth(16)) rom_1 (.addr(PC_q), .data(rom_1_data), .sel(1'b1));
  Hex_Digit_Display hex_digit_display_1 (.value(register_1_q));  // open: dp
  Shifter Shifter (
    .Shamt(Fields_shamt), .Rt(Registers_read_data_1), .Rs(Decoder_p6), .SubOp(Fields_subop),
    .Immediate(Fields_opcode[3]));  // open: Output
  Register #(.width(16)) register_1 (
    .D(Registers_read_data_1), .en(Decoder_p7), .Q({register_1_q_3, register_1_q_2, register_1_q}),
    .clk(Clock_out));  // open: clr
  Hex_Digit_Display hex_digit_display_2 (.value(register_1_q_2));  // open: dp
  Fields Fields (
    .Input(rom_1_data), .Opcode(Fields_opcode), .Subop(Fields_subop), .Shamt(Fields_shamt), .Imm(Fields_imm),
    .RS(Fields_rs), .RT(Fields_rt));
  Hex_Digit_Display hex_digit_display_3 (.value(register_1_q_3[11:8]));  // open: dp
  // Decoder Decoder: pin names not known; wires that end beside it: Fields_subop, Fields_opcode[3], Fields_subop, Decoder_p4, Decoder_p5, Decoder_p6, Decoder_p7, Decoder_p8, Decoder_p9, Decoder_p10, Decoder_p11[0], Decoder_p11[1], Decoder_p13
  Sign_Extend Sign_Extend (.Input(Fields_imm), .Output(Sign_Extend_output));  // open: Sign
  Hex_Digit_Display hex_digit_display_4 (.value(register_1_q_3[15:12]));  // open: dp
  Register_File Registers (
    .Read_1(Fields_rs), .Read_2(Fields_rt), .Write(Fields_rs), .Write_Data(multiplexer_3_out),
    .RegWrite(Clock_out), .Clock(Decoder_p9), .Read_Data_1(Registers_read_data_1), .Read_Data_2(Decoder_p6));
  Multiplexer #(.width(16), .enable("false")) multiplexer_2 (
    .in0(Decoder_p6), .in1(Sign_Extend_output), .out(multiplexer_2_out), .sel(Decoder_p10));
  ALU ALU (
    .A(Registers_read_data_1), .B(multiplexer_2_out), .Operation(Decoder_p11),
    .Result({ALU_result_2, ALU_result}));
  RAM #(.dataWidth(16), .bus("separate")) ram_1 (
    .addr(ALU_result), .din(Registers_read_data_1), .data(ram_1_data), .str(Decoder_p13), .clk(Clock_out),
    .ld(Decoder_p6[0]), .clr(1'b1));  // open: sel
  Multiplexer #(.width(16), .enable("false")) multiplexer_3 (
    .in0(ram_1_data), .in1({ALU_result_2, ALU_result}), .out(multiplexer_3_out), .sel(Decoder_p8));
  // Pins of 1 and 16 bits meet at Decoder_p6

  // Notes on the sheet:
  //   contents of rom_1 (hex, n*v repeats v):
  //   4*2345
endmodule

module Register_File (
  input  [2:0] Read_1,
  input  [2:0] Read_2,
  input  RegWrite,
  input  [2:0] Write,
  input  [15:0] Write_Data,
  input  Clock,
  output [15:0] Read_Data_1,
  output [15:0] Read_Data_2
);

  wire [15:0] demultiplexer_1_out0, demultiplexer_1_out1, demultiplexer_1_out2, demultiplexer_1_out3,
       demultiplexer_1_out4, demultiplexer_1_out5, demultiplexer_1_out6, demultiplexer_1_out7, Reg_1_q,
       Reg_2_q, Reg_3_q, Reg_4_q, Reg_5_q, Reg_7_q, Reg_8_q;

  Demultiplexer #(.select(3), .width(16)) demultiplexer_1 (
    .out0(demultiplexer_1_out0), .out1(demultiplexer_1_out1), .out2(demultiplexer_1_out2),
    .out3(demultiplexer_1_out3), .out4(demultiplexer_1_out4), .out5(demultiplexer_1_out5),
    .out6(demultiplexer_1_out6), .out7(demultiplexer_1_out7), .in(Write_Data), .sel(Write), .en(RegWrite));
  Register #(.width(16)) Reg_1 (.D(demultiplexer_1_out0), .Q(Reg_1_q), .clk(Clock));  // open: en, clr
  Register #(.width(16)) Reg_2 (.D(demultiplexer_1_out1), .Q(Reg_2_q), .clk(Clock));  // open: en, clr
  Register #(.width(16)) Reg_3 (.D(demultiplexer_1_out2), .Q(Reg_3_q), .clk(Clock));  // open: en, clr
  Register #(.width(16)) Reg_4 (.D(demultiplexer_1_out3), .Q(Reg_4_q), .clk(Clock));  // open: en, clr
  Register #(.width(16)) Reg_5 (.D(demultiplexer_1_out4), .Q(Reg_5_q), .clk(Clock));  // open: en, clr
  Register #(.width(16)) Reg_6 (.D(demultiplexer_1_out5), .Q(Reg_5_q), .clk(Clock));  // open: en, clr
  Register #(.width(16)) Reg_7 (.D(demultiplexer_1_out6), .Q(Reg_7_q), .clk(Clock));  // open: en, clr
  Register #(.width(16)) Reg_8 (.D(demultiplexer_1_out7), .Q(Reg_8_q), .clk(Clock));  // open: en, clr
  Multiplexer #(.select(3), .width(16), .enable("false")) multiplexer_1 (
    .in0(Reg_1_q), .in1(Reg_2_q), .in2(Reg_3_q), .in3(Reg_4_q), .in4(Reg_5_q), .in5(Reg_5_q), .in6(Reg_7_q),
    .in7(Reg_8_q), .out(Read_Data_1), .sel(Read_1));
  Multiplexer #(.select(3), .width(16), .enable("false")) multiplexer_2 (
    .in0(Reg_1_q), .in1(Reg_2_q), .in2(Reg_3_q), .in3(Reg_4_q), .in4(Reg_5_q), .in5(Reg_5_q), .in6(Reg_7_q),
    .in7(Reg_8_q), .out(Read_Data_2), .sel(Read_2));
endmodule

module Fields (
  input  [15:0] Input,
  output [3:0] Opcode,
  output Subop,
  output [3:0] Shamt,
  output [7:0] Imm,
  output [2:0] RS,
  output [2:0] RT
);


  assign Imm = Input[8:1];
  assign Opcode = Input[15:12];
  assign RS = Input[11:9];
  assign RT = Input[8:6];
  assign Shamt = Input[4:1];
  assign Subop = Input[0];
endmodule

module ALU (
  input  [1:0] Operation,
  input  [15:0] A,
  input  [15:0] B,
  output [15:0] Result
);

  wire [15:0] adder_1_out, and_1_out, nor_1_out, subtractor_1_out;

  Adder #(.width(16)) adder_1 (.a(A), .b(B), .out(adder_1_out), .cin(1'b0));  // open: cout
  Subtractor #(.width(16)) subtractor_1 (.a(A), .b(B), .out(subtractor_1_out), .bin(1'b0));  // open: bout
  assign nor_1_out = ~(A | B);  // NOR_Gate nor_1, 16 bits wide
  assign and_1_out = A & B;  // AND_Gate and_1, 16 bits wide
  Multiplexer #(.select(2), .width(16), .enable("false")) multiplexer_1 (
    .in0(adder_1_out), .in1(subtractor_1_out), .in2(nor_1_out), .in3(and_1_out), .out(Result), .sel(Operation));
endmodule

module Decoder (
  input  OPC0,
  input  OPC1,
  input  OPC2,
  input  OPC3,
  input  SubOp,
  output Halt,
  output Branch,
  output Put,
  output MemToReg,
  output RegWrite,
  output ALUsrc,
  output ALUOP1,
  output ALUOP2,
  output MemWrite,
  output MemRead
);

  wire and_1_out, and_2_out, and_3_out, and_4_out, and_5_out, and_6_out, and_7_out, and_8_out, and_9_out,
       not_1_out, not_2_out, not_3_out, not_4_out, not_5_out, not_6_out, not_7_out, not_8_out, not_9_out,
       not_10_out, not_11_out, not_12_out, not_13_out, not_14_out, not_15_out, not_16_out;

  not not_1 (not_1_out, OPC0);
  not not_2 (not_2_out, OPC1);
  not not_3 (not_3_out, OPC3);
  not not_4 (not_4_out, OPC0);
  not not_5 (not_5_out, OPC1);
  not not_6 (not_6_out, OPC2);
  not not_7 (not_7_out, OPC3);
  not not_8 (not_8_out, OPC3);
  not not_9 (not_9_out, OPC3);
  not not_10 (not_10_out, OPC2);
  not not_11 (not_11_out, OPC3);
  not not_12 (not_12_out, SubOp);
  not not_13 (not_13_out, OPC3);
  not not_14 (not_14_out, SubOp);
  not not_15 (not_15_out, OPC3);
  not not_16 (not_16_out, SubOp);
  and and_1 (and_1_out, not_1_out, not_2_out, OPC2, not_3_out);
  and and_2 (and_2_out, not_4_out, not_5_out, OPC2, SubOp);
  and and_3 (and_3_out, not_6_out, not_7_out);
  and and_4 (and_4_out, OPC1, not_8_out);
  and and_5 (and_5_out, OPC0, not_9_out);
  and and_6 (and_6_out, not_10_out, not_11_out, not_12_out);
  and and_7 (and_7_out, OPC3, SubOp);
  and and_8 (and_8_out, OPC1, not_13_out, not_14_out);
  and and_9 (and_9_out, OPC0, not_15_out, not_16_out);
  or or_1 (ALUsrc, and_1_out, and_2_out);
  or or_2 (ALUOP1, and_3_out, and_4_out, and_5_out);
  or or_3 (ALUOP2, and_6_out, and_7_out, and_8_out, and_9_out);

  assign MemRead = 1'b0;
  assign MemToReg = 1'b1;
  assign MemWrite = 1'b0;
  assign RegWrite = 1'b1;
endmodule

module Shifter (
  input  [3:0] Shamt,
  input  [15:0] Rt,
  input  [15:0] Rs,
  input  SubOp,
  input  Immediate,
  output [15:0] Output
);

  wire not_1_out;
  wire [3:0] multiplexer_1_out, multiplexer_2_out;
  wire [15:0] shifter_1_out, shifter_2_out;

  not not_1 (not_1_out, Immediate);
  Multiplexer #(.width(4), .enable("false")) multiplexer_1 (
    .in0(Shamt), .in1(Rt[3:0]), .out(multiplexer_1_out), .sel(not_1_out));
  Multiplexer #(.width(4), .enable("false")) multiplexer_2 (
    .in0(Shamt), .in1(Rt[3:0]), .out(multiplexer_2_out), .sel(not_1_out));
  Shifter_part #(.width(16)) shifter_1 (.in(Rs), .\dist (multiplexer_1_out), .out(shifter_1_out));
  Shifter_part #(.width(16), .shift("lr")) shifter_2 (.in(Rs), .\dist (multiplexer_2_out), .out(shifter_2_out));
  Multiplexer #(.width(16), .enable("false")) multiplexer_3 (
    .in0(shifter_1_out), .in1(shifter_2_out), .out(Output), .sel(SubOp));
endmodule

module Decoder2 (
  input  OPC0,
  input  OPC1,
  input  OPC2,
  input  OPC3,
  input  SubOp,
  output Halt,
  output Branch,
  output Put
);

  wire and_1_out, and_2_out, not_1_out, not_2_out;

  not not_1 (not_1_out, OPC0);
  not not_2 (not_2_out, OPC3);
  and and_1 (and_1_out, not_1_out, OPC1, OPC2, not_2_out);
  and and_2 (and_2_out, OPC0, OPC1, OPC2, OPC3);
  or or_1 (Halt, and_1_out, and_2_out);
endmodule

module Sign_Extend (
  input  Sign,
  input  [7:0] Input,
  output [15:0] Output
);

  wire [15:0] bit_extender_1_out, bit_extender_2_out;

  assign bit_extender_1_out = {{8{1'b0}}, Input};  // Bit_Extender bit_extender_1
  assign bit_extender_2_out = {{8{Input[7]}}, Input};  // Bit_Extender bit_extender_2
  Multiplexer #(.width(16), .enable("false")) multiplexer_1 (
    .in0(bit_extender_1_out), .in1(bit_extender_2_out), .out(Output), .sel(Sign));
endmodule
